// Logisim project Half_Adder_MUX.circ as structural Verilog: 1 circuit, main circuit main
module main (
  input  _0,
  input  _0_2,
  input  S_1,
  input  C_1,
  input  [1:0] A_B,
  output Y,
  output Y_2
);

  Multiplexer #(.select(2)) multiplexer_1 (.in0(_0), .in1(S_1), .in2(S_1), .in3(_0), .out(Y), .sel(A_B));  // open: en
  Multiplexer #(.select(2)) multiplexer_2 (
    .in0(_0_2), .in1(_0_2), .in2(_0_2), .in3(C_1), .out(Y_2), .sel(A_B));  // open: en

  // Notes on the sheet:
  //   SUM
  //   CARRY
endmodule
