// Logisim project 5-bit_parallel_adder.circ as structural Verilog: 2 circuits, main circuit main
module main (
  input  A,
  input  B,
  input  Cin,
  output SUM__S,
  output CARRY__C
);

  wire and_1_out, and_2_out, xor_1_out;

  xor xor_1 (xor_1_out, A, B);
  and and_1 (and_1_out, A, B);
  and and_2 (and_2_out, xor_1_out, Cin);
  xor xor_2 (SUM__S, xor_1_out, Cin);
  or or_1 (CARRY__C, and_1_out, and_2_out);
endmodule

module _5_BIT_PARALLEL_ADDER (
  input  in_1,
  input  A4,
  input  A3,
  input  A2,
  input  A1,
  input  A0,
  input  B4,
  input  B3,
  input  B2,
  input  B1,
  input  B0,
  output out_12,
  output out_13,
  output out_14,
  output out_15,
  output out_16,
  output out_17
);

  wire main_2_carry__c, main_3_carry__c, main_4_carry__c, main_5_carry__c;

  main main_1 (.A(B4), .B(A4), .Cin(main_2_carry__c), .SUM__S(out_13), .CARRY__C(out_12));
  main main_2 (.A(B3), .B(A3), .Cin(main_3_carry__c), .SUM__S(out_14), .CARRY__C(main_2_carry__c));
  main main_3 (.A(B2), .B(A2), .Cin(main_4_carry__c), .SUM__S(out_15), .CARRY__C(main_3_carry__c));
  main main_4 (.A(B1), .B(A1), .Cin(main_5_carry__c), .SUM__S(out_16), .CARRY__C(main_4_carry__c));
  main main_5 (.A(B0), .B(A0), .Cin(in_1), .SUM__S(out_17), .CARRY__C(main_5_carry__c));
endmodule
