// Logisim project Johnson_counter.circ as structural Verilog: 1 circuit, main circuit main
module main (
  input  in_1,
  output out_2,
  output out_3,
  output out_4
);

  wire clock_1_out, d_ff_3_qn;

  Clock clock_1 (.out(clock_1_out));
  D_Flip_Flop d_ff_1 (.clk(clock_1_out), .D(d_ff_3_qn), .Q(out_2), .reset(in_1));  // open: Qn, preset, en
  D_Flip_Flop d_ff_2 (.clk(clock_1_out), .D(out_2), .Q(out_3), .reset(in_1));  // open: Qn, preset, en
  D_Flip_Flop d_ff_3 (.clk(clock_1_out), .D(out_3), .Q(out_4), .Qn(d_ff_3_qn), .reset(in_1));  // open: preset, en
endmodule
