// Logisim project 3-bit_ripple_counter-seven-segment-display_integrated.circ as structural Verilog: 2 circuits, main circuit main
module main (
  input  RESET
);

  wire clock_1_out, f_1_y1, f_1_y2, f_1_y3, f_1_y4, f_1_y5, f_1_y6, f_1_y7, j_k_ff_1_q, j_k_ff_2_q,
       j_k_ff_3_q;

  Clock clock_1 (.out(clock_1_out));
  J_K_Flip_Flop #(.trigger("falling")) j_k_ff_1 (
    .J(1'b1), .clk(clock_1_out), .K(1'b1), .Q(j_k_ff_1_q), .reset(RESET));  // open: Qn, preset, en
  J_K_Flip_Flop #(.trigger("falling")) j_k_ff_2 (
    .J(1'b1), .clk(j_k_ff_1_q), .K(1'b1), .Q(j_k_ff_2_q), .reset(RESET));  // open: Qn, preset, en
  J_K_Flip_Flop #(.trigger("falling")) j_k_ff_3 (
    .J(1'b1), .clk(j_k_ff_2_q), .K(1'b1), .Q(j_k_ff_3_q), .reset(RESET));  // open: Qn, preset, en
  F f_1 (
    .A2(j_k_ff_3_q), .A1(j_k_ff_2_q), .A0(j_k_ff_1_q), .Y7(f_1_y7), .Y6(f_1_y6), .Y5(f_1_y5), .Y4(f_1_y4),
    .Y3(f_1_y3), .Y2(f_1_y2), .Y1(f_1_y1));
  _7_Segment_Display u_7_segment_display_1 (
    .g(f_1_y1), .f(f_1_y3), .a(f_1_y2), .b(f_1_y7), .e(f_1_y4), .d(f_1_y5), .c(f_1_y6));  // open: dp

  // Notes on the sheet:
  //   J&K
  //   CLOCK
endmodule

module F (
  input  A2,
  input  A1,
  input  A0,
  output Y7,
  output Y6,
  output Y5,
  output Y4,
  output Y3,
  output Y2,
  output Y1
);

  wire and_1_out, and_2_out, and_3_out, and_4_out, and_5_out, and_6_out, and_7_out, and_8_out, not_1_out,
       not_2_out, not_3_out;

  not not_1 (not_1_out, A2);
  not not_2 (not_2_out, A0);
  not not_3 (not_3_out, A1);
  and and_1 (and_1_out, not_1_out, not_3_out, not_2_out);
  and and_2 (and_2_out, not_1_out, not_3_out, A0);
  and and_3 (and_3_out, not_1_out, A1, not_2_out);
  and and_4 (and_4_out, not_1_out, A1, A0);
  and and_5 (and_5_out, A2, not_3_out, not_2_out);
  and and_6 (and_6_out, A2, not_3_out, A0);
  and and_7 (and_7_out, A2, A1, not_2_out);
  and and_8 (and_8_out, A2, A1, A0);
  or or_1 (Y7, and_1_out, and_2_out, and_3_out, and_5_out, and_8_out, and_4_out);
  or or_2 (Y6, and_1_out, and_2_out, and_4_out, and_5_out, and_6_out, and_7_out, and_8_out);
  or or_3 (Y5, and_1_out, and_3_out, and_4_out, and_6_out, and_7_out);
  or or_4 (Y4, and_1_out, and_3_out, and_7_out);
  or or_5 (Y3, and_1_out, and_5_out, and_6_out, and_7_out);
  or or_6 (Y2, and_1_out, and_3_out, and_4_out, and_6_out, and_7_out, and_8_out);
  or or_7 (Y1, and_3_out, and_4_out, and_5_out, and_6_out, and_7_out);
endmodule
