// Logisim project 4-bit_ripple_counter-seven-segment-display_integrated.circ as structural Verilog: 3 circuits, main circuit main
module main (
  input  D,
  input  C,
  input  B,
  input  A,
  output Y15,
  output Y14,
  output Y13,
  output Y12,
  output Y11,
  output Y10,
  output Y9,
  output Y8,
  output Y7,
  output Y6,
  output Y5,
  output Y4,
  output Y3,
  output Y2,
  output Y1,
  output Y0
);

  wire not_1_out, not_2_out, not_3_out, not_4_out;

  not not_1 (not_1_out, D);
  not not_2 (not_2_out, C);
  not not_3 (not_3_out, A);
  not not_4 (not_4_out, B);
  and and_1 (Y15, not_1_out, not_2_out, not_4_out, not_3_out);
  and and_2 (Y14, not_1_out, not_2_out, not_4_out, A);
  and and_3 (Y13, not_1_out, not_2_out, B, not_3_out);
  and and_4 (Y12, not_1_out, not_2_out, B, A);
  and and_5 (Y11, not_1_out, C, not_4_out, not_3_out);
  and and_6 (Y10, not_1_out, C, not_4_out, A);
  and and_7 (Y9, not_1_out, C, B, not_3_out);
  and and_8 (Y8, not_1_out, C, B, A);
  and and_9 (Y7, D, not_2_out, not_4_out, not_3_out);
  and and_10 (Y6, D, not_2_out, not_4_out, A);
  and and_11 (Y5, D, not_2_out, B, not_3_out);
  and and_12 (Y4, D, not_2_out, B, A);
  and and_13 (Y3, D, C, not_4_out, not_3_out);
  and and_14 (Y2, D, C, not_4_out, A);
  and and_15 (Y1, D, C, B, not_3_out);
  and and_16 (Y0, D, C, B, A);
endmodule

module counter (
  input  RESET
);

  wire clock_1_out, decoder_1_y3, decoder_1_y4, decoder_1_y5, decoder_1_y6, decoder_1_y7, decoder_1_y8,
       decoder_1_y9, decoder_1_y10, decoder_1_y11, decoder_1_y12, decoder_1_y13, decoder_1_y14,
       decoder_1_y15, j_k_ff_1_q, j_k_ff_2_q, j_k_ff_3_q, j_k_ff_4_q;

  Clock clock_1 (.out(clock_1_out));
  J_K_Flip_Flop #(.trigger("falling")) j_k_ff_1 (
    .J(1'b1), .clk(clock_1_out), .K(1'b1), .Q(j_k_ff_1_q), .reset(RESET));  // open: Qn, preset, en
  J_K_Flip_Flop #(.trigger("falling")) j_k_ff_2 (
    .J(1'b1), .clk(j_k_ff_1_q), .K(1'b1), .Q(j_k_ff_2_q), .reset(RESET));  // open: Qn, preset, en
  J_K_Flip_Flop #(.trigger("falling")) j_k_ff_3 (
    .J(1'b1), .clk(j_k_ff_2_q), .K(1'b1), .Q(j_k_ff_3_q), .reset(RESET));  // open: Qn, preset, en
  J_K_Flip_Flop #(.trigger("falling")) j_k_ff_4 (
    .J(1'b1), .clk(j_k_ff_3_q), .K(1'b1), .Q(j_k_ff_4_q), .reset(RESET));  // open: Qn, preset, en
  decoder decoder_1 (
    .A3(j_k_ff_4_q), .A2(j_k_ff_3_q), .A0(j_k_ff_2_q), .in_4(j_k_ff_1_q), .Y15(decoder_1_y15),
    .Y14(decoder_1_y14), .Y13(decoder_1_y13), .Y12(decoder_1_y12), .Y11(decoder_1_y11), .Y10(decoder_1_y10),
    .Y9(decoder_1_y9), .Y8(decoder_1_y8), .Y7(decoder_1_y7), .Y6(decoder_1_y6), .Y5(decoder_1_y5),
    .Y4(decoder_1_y4), .Y3(decoder_1_y3));
  _7_Segment_Display u_7_segment_display_1 (
    .f(decoder_1_y11), .a(decoder_1_y10), .b(decoder_1_y15), .e(decoder_1_y12), .d(decoder_1_y13),
    .c(decoder_1_y14));  // open: g, dp
  _7_Segment_Display u_7_segment_display_2 (
    .g(decoder_1_y3), .f(decoder_1_y5), .a(decoder_1_y4), .b(decoder_1_y9), .e(decoder_1_y6),
    .d(decoder_1_y7), .c(decoder_1_y8));  // open: dp

  // Notes on the sheet:
  //   J&K
  //   CLOCK
endmodule

module decoder (
  input  A3,
  input  A2,
  input  A0,
  input  in_4,
  output Y15,
  output Y14,
  output Y13,
  output Y12,
  output Y11,
  output Y10,
  output Y9,
  output Y8,
  output Y7,
  output Y6,
  output Y5,
  output Y4,
  output Y3
);

  wire main_1_y0, main_1_y1, main_1_y2, main_1_y3, main_1_y4, main_1_y5, main_1_y6, main_1_y7, main_1_y8,
       main_1_y9, main_1_y10, main_1_y11, main_1_y12, main_1_y13, main_1_y14, main_1_y15;

  main main_1 (
    .D(A3), .C(A2), .B(A0), .A(in_4), .Y15(main_1_y15), .Y14(main_1_y14), .Y13(main_1_y13), .Y12(main_1_y12),
    .Y11(main_1_y11), .Y10(main_1_y10), .Y9(main_1_y9), .Y8(main_1_y8), .Y7(main_1_y7), .Y6(main_1_y6),
    .Y5(main_1_y5), .Y4(main_1_y4), .Y3(main_1_y3), .Y2(main_1_y2), .Y1(main_1_y1), .Y0(main_1_y0));
  or or_1 (Y15, main_1_y8, main_1_y15, main_1_y14, main_1_y13, main_1_y12, main_1_y11, main_1_y10, main_1_y9, main_1_y7, main_1_y6, main_1_y5, main_1_y4, main_1_y3, main_1_y2, main_1_y1, main_1_y0);
  or or_2 (Y14, main_1_y8, main_1_y15, main_1_y14, main_1_y13, main_1_y12, main_1_y11, main_1_y10, main_1_y9, main_1_y7, main_1_y6, main_1_y5, main_1_y4, main_1_y3, main_1_y2, main_1_y1, main_1_y0);
  or or_3 (Y13, main_1_y15, main_1_y14, main_1_y13, main_1_y12, main_1_y11, main_1_y10, main_1_y9, main_1_y8, main_1_y7, main_1_y6);
  or or_4 (Y12, main_1_y15, main_1_y14, main_1_y13, main_1_y12, main_1_y11, main_1_y10, main_1_y9, main_1_y8, main_1_y7, main_1_y6);
  or or_5 (Y11, main_1_y15, main_1_y14, main_1_y13, main_1_y12, main_1_y11, main_1_y10, main_1_y9, main_1_y8, main_1_y7, main_1_y6);
  or or_6 (Y10, main_1_y15, main_1_y14, main_1_y13, main_1_y12, main_1_y11, main_1_y10, main_1_y9, main_1_y8, main_1_y7, main_1_y6);
  or or_7 (Y9, main_1_y1, main_1_y15, main_1_y14, main_1_y13, main_1_y12, main_1_y11, main_1_y4, main_1_y5, main_1_y8, main_1_y7, main_1_y6, main_1_y3, main_1_y2);
  or or_8 (Y8, main_1_y8, main_1_y15, main_1_y14, main_1_y12, main_1_y11, main_1_y10, main_1_y9, main_1_y7, main_1_y6, main_1_y5, main_1_y4, main_1_y2, main_1_y1, main_1_y0);
  or or_9 (Y7, main_1_y13, main_1_y12, main_1_y10, main_1_y9, main_1_y7, main_1_y6, main_1_y5, main_1_y3, main_1_y2, main_1_y0, main_1_y15);
  or or_10 (Y6, main_1_y15, main_1_y13, main_1_y9, main_1_y5, main_1_y3, main_1_y7);
  or or_11 (Y3, main_1_y13, main_1_y12, main_1_y11, main_1_y10, main_1_y9, main_1_y7, main_1_y6, main_1_y3, main_1_y2, main_1_y1, main_1_y0);
  or or_12 (Y5, main_1_y8, main_1_y15, main_1_y11, main_1_y10, main_1_y9, main_1_y7, main_1_y6, main_1_y5, main_1_y1, main_1_y0);
  or or_13 (Y4, main_1_y15, main_1_y13, main_1_y12, main_1_y10, main_1_y9, main_1_y8, main_1_y6, main_1_y5, main_1_y3, main_1_y2, main_1_y0, main_1_y7);

  // Notes on the sheet:
  //   A1
endmodule
