// Logisim project wallace_tree_multiplier.circ as structural Verilog: 3 circuits, main circuit main
module main (
  input  A3,
  input  A2,
  input  A1,
  input  A0,
  input  B3,
  input  B2,
  input  B1,
  input  B0,
  output out_9,
  output out_10,
  output out_11,
  output out_12,
  output out_13,
  output out_14,
  output out_15,
  output out_16
);

  wire and_1_out, and_2_out, and_3_out, and_4_out, and_5_out, and_6_out, and_7_out, and_8_out, and_9_out,
       and_10_out, and_11_out, and_12_out, and_13_out, and_14_out, and_16_out, fa_2_out_5, fa_3_out_4,
       fa_3_out_5, fa_4_out_5, fa_5_out_4, fa_5_out_5, fa_6_out_4, fa_6_out_5, fa_7_out_4, fa_7_out_5,
       fa_8_out_4, fa_8_out_5, ha_1_out_3, ha_1_out_4, ha_2_out_4, ha_3_out_4, ha_4_out_4;

  FA fa_1 (.in_1(fa_3_out_5), .in_2(fa_2_out_5), .in_3(and_1_out), .out_4(out_10), .out_5(out_9));
  FA fa_2 (.in_1(fa_4_out_5), .in_2(fa_3_out_4), .in_3(fa_5_out_5), .out_4(out_11), .out_5(fa_2_out_5));
  and and_1 (and_1_out, B3, A3);
  FA fa_3 (.in_1(and_5_out), .in_2(ha_1_out_4), .in_3(and_2_out), .out_4(fa_3_out_4), .out_5(fa_3_out_5));
  FA fa_4 (.in_1(ha_2_out_4), .in_2(fa_7_out_5), .in_3(fa_5_out_4), .out_4(out_12), .out_5(fa_4_out_5));
  and and_2 (and_2_out, B3, A2);
  FA fa_5 (.in_1(and_3_out), .in_2(fa_6_out_5), .in_3(ha_1_out_3), .out_4(fa_5_out_4), .out_5(fa_5_out_5));
  and and_3 (and_3_out, B3, A1);
  and and_4 (and_4_out, B3, A0);
  HA ha_1 (.in_1(and_6_out), .in_2(and_10_out), .out_3(ha_1_out_3), .out_4(ha_1_out_4));
  HA ha_2 (.in_1(ha_3_out_4), .in_2(fa_7_out_4), .out_3(out_13), .out_4(ha_2_out_4));
  and and_5 (and_5_out, B2, A3);
  FA fa_6 (.in_1(and_7_out), .in_2(and_9_out), .in_3(and_14_out), .out_4(fa_6_out_4), .out_5(fa_6_out_5));
  FA fa_7 (.in_1(fa_6_out_4), .in_2(fa_8_out_5), .in_3(and_4_out), .out_4(fa_7_out_4), .out_5(fa_7_out_5));
  and and_6 (and_6_out, B2, A2);
  and and_7 (and_7_out, B2, A1);
  HA ha_3 (.in_1(ha_4_out_4), .in_2(fa_8_out_4), .out_3(out_14), .out_4(ha_3_out_4));
  and and_8 (and_8_out, B2, A0);
  FA fa_8 (.in_1(and_8_out), .in_2(and_11_out), .in_3(and_13_out), .out_4(fa_8_out_4), .out_5(fa_8_out_5));
  and and_9 (and_9_out, B1, A2);
  and and_10 (and_10_out, B1, A3);
  and and_11 (and_11_out, B1, A1);
  HA ha_4 (.in_1(and_16_out), .in_2(and_12_out), .out_3(out_15), .out_4(ha_4_out_4));
  and and_12 (and_12_out, B1, A0);
  and and_13 (and_13_out, B0, A2);
  and and_14 (and_14_out, B0, A3);
  and and_15 (out_16, B0, A0);
  and and_16 (and_16_out, B0, A1);

  // Notes on the sheet:
  //   P15
  //   C8
  //   S8
  //   P14
  //   S4
  //   S7
  //   C7
  //   P12
  //   P13
  //   C4
  //   C6
  //   S6
  //   P11
  //   C3
  //   S3
  //   P10
  //   P9
  //   C5
  //   S5
  //   P8
  //   C2
  //   S2
  //   P7
  //   C1
  //   P5
  //   P6
  //   S1
  //   P4
  //   P3
  //   P2
  //   P1
  //   P0
endmodule

module FA (
  input  in_1,
  input  in_2,
  input  in_3,
  output out_4,
  output out_5
);

  wire and_1_out, and_2_out, xor_1_out;

  xor xor_1 (xor_1_out, in_1, in_2);
  xor xor_2 (out_4, xor_1_out, in_3);
  and and_1 (and_1_out, xor_1_out, in_3);
  and and_2 (and_2_out, in_1, in_2);
  or or_1 (out_5, and_1_out, and_2_out);
endmodule

module HA (
  input  in_1,
  input  in_2,
  output out_3,
  output out_4
);

  xor xor_1 (out_3, in_1, in_2);
  and and_1 (out_4, in_1, in_2);
endmodule
