// Logisim project bidirectional_PISO_shift_register.circ as structural Verilog: 1 circuit, main circuit main
module main (
  input  X,
  input  in_2,
  input  in_3,
  input  CLEAR,
  output CLK,
  output out_6
);

  wire and_1_out, and_2_out, and_3_out, and_4_out, and_5_out, and_6_out, and_7_out, and_8_out, button_1_out,
       d_ff_2_q, d_ff_3_q, not_1_out, or_1_out, or_2_out, or_3_out, or_4_out;

  Button button_1 (.out(button_1_out));
  not not_1 (not_1_out, X);
  and and_1 (and_1_out, in_2, X);
  or or_1 (or_1_out, and_1_out, and_2_out);
  and and_2 (and_2_out, not_1_out, d_ff_2_q);
  D_Flip_Flop d_ff_1 (.clk(button_1_out), .D(or_1_out), .Q(CLK), .reset(CLEAR));  // open: Qn, preset, en
  and and_3 (and_3_out, CLK, X);
  or or_2 (or_2_out, and_3_out, and_4_out);
  and and_4 (and_4_out, not_1_out, d_ff_3_q);
  D_Flip_Flop d_ff_2 (.clk(button_1_out), .D(or_2_out), .Q(d_ff_2_q), .reset(CLEAR));  // open: Qn, preset, en
  and and_5 (and_5_out, not_1_out, out_6);
  and and_6 (and_6_out, d_ff_2_q, X);
  or or_3 (or_3_out, and_6_out, and_5_out);
  D_Flip_Flop d_ff_3 (.clk(button_1_out), .D(or_3_out), .Q(d_ff_3_q), .reset(CLEAR));  // open: Qn, preset, en
  and and_7 (and_7_out, d_ff_3_q, X);
  or or_4 (or_4_out, and_7_out, and_8_out);
  and and_8 (and_8_out, not_1_out, in_3);
  D_Flip_Flop d_ff_4 (.clk(button_1_out), .D(or_4_out), .Q(out_6), .reset(CLEAR));  // open: Qn, preset, en

  // Notes on the sheet:
  //   OUTPUT (RIGHT TO LEFT)
  //   (INPUT LEFT TO RIGHT)
  //   X = 0 LEFT TO RIGHT PARALLEL INPUT SERIAL OUTPUT (PISO) REGISTER
  //   X = 1 RIGHT TO LEFT PARALLEL INPUT SERIAL OUTPUT (PISO) REGISTER
  //   BIDIRECTIONAL PISO SHIFT REGISTER
  //   INPUT ( RIGHT TO LEFT )
  //   OUTPUT ( LEFT TO RIGHT)
endmodule
