// Logisim project 4-bit_parallel_subtractor_using_HS.circ as structural Verilog: 2 circuits, main circuit main
module main (
  input  A,
  input  B,
  input  bin,
  output Difference,
  output Bout
);

  wire and_1_out, and_2_out, not_1_out, not_2_out, xor_1_out;

  xor xor_1 (xor_1_out, A, B);
  and and_1 (and_1_out, B, not_1_out);
  not not_1 (not_1_out, A);
  not not_2 (not_2_out, xor_1_out);
  xor xor_2 (Difference, xor_1_out, bin);
  and and_2 (and_2_out, not_2_out, bin);
  or or_1 (Bout, and_2_out, and_1_out);
endmodule

module _4_BIT_PARALLEL_SUBTRACTOR_USING_FS (
  input  in_1,
  input  B3,
  input  B2,
  input  B1,
  input  B0,
  input  A3,
  input  A2,
  input  A1,
  input  A0,
  output out_10,
  output S3,
  output S2,
  output S1,
  output S0
);

  wire main_2_bout, main_3_bout, main_4_bout;

  main main_1 (.A(A3), .B(B3), .bin(main_2_bout), .Difference(S3), .Bout(out_10));
  main main_2 (.A(A2), .B(B2), .bin(main_3_bout), .Difference(S2), .Bout(main_2_bout));
  main main_3 (.A(A1), .B(B1), .bin(main_4_bout), .Difference(S1), .Bout(main_3_bout));
  main main_4 (.A(A0), .B(B0), .bin(in_1), .Difference(S0), .Bout(main_4_bout));

  // Notes on the sheet:
  //   SUBTRACT B FROM A
endmodule
