// Logisim project 5-bit_parallel_subtractor.circ as structural Verilog: 2 circuits, main circuit main
module main (
  input  A,
  input  B,
  input  bin,
  output DIFFERENCE__D,
  output BORROW__B
);

  wire and_1_out, and_2_out, not_1_out, not_2_out, xor_1_out;

  xor xor_1 (xor_1_out, A, B);
  not not_1 (not_1_out, A);
  not not_2 (not_2_out, xor_1_out);
  and and_1 (and_1_out, not_1_out, B);
  and and_2 (and_2_out, not_2_out, bin);
  xor xor_2 (DIFFERENCE__D, xor_1_out, bin);
  or or_1 (BORROW__B, and_1_out, and_2_out);
endmodule

module _5_BIT_PARALLEL_SUBTRACTOR (
  input  in_1,
  input  B0,
  input  B1,
  input  B2,
  input  A0,
  input  B3,
  input  A1,
  input  B4,
  input  A2,
  input  A3,
  input  A4,
  output out_12,
  output out_13,
  output out_14,
  output out_15,
  output out_16,
  output out_17
);

  wire main_2_borrow__b, main_3_borrow__b, main_4_borrow__b, main_5_borrow__b;

  main main_1 (.A(A4), .B(B4), .bin(main_2_borrow__b), .DIFFERENCE__D(out_13), .BORROW__B(out_12));
  main main_2 (.A(A3), .B(B3), .bin(main_3_borrow__b), .DIFFERENCE__D(out_14), .BORROW__B(main_2_borrow__b));
  main main_3 (.A(A2), .B(B2), .bin(main_4_borrow__b), .DIFFERENCE__D(out_15), .BORROW__B(main_3_borrow__b));
  main main_4 (.A(A1), .B(B1), .bin(main_5_borrow__b), .DIFFERENCE__D(out_16), .BORROW__B(main_4_borrow__b));
  main main_5 (.A(A0), .B(B0), .bin(in_1), .DIFFERENCE__D(out_17), .BORROW__B(main_5_borrow__b));
endmodule
