// Logisim project full_subtractor_using_8x1_mux.circ as structural Verilog: 1 circuit, main circuit main
module main (
  input  _0,
  input  _0_2,
  input  D_1,
  input  Bout_1,
  input  [2:0] A_B_C,
  output Y,
  output Y_2
);

  Multiplexer #(.select(3)) multiplexer_1 (
    .in0(_0), .in1(D_1), .in2(D_1), .in3(_0), .in4(D_1), .in5(_0), .in6(_0), .in7(D_1), .out(Y), .sel(A_B_C));  // open: en
  Multiplexer #(.select(3)) multiplexer_2 (
    .in0(_0_2), .in1(Bout_1), .in2(Bout_1), .in3(Bout_1), .in4(_0_2), .in5(_0_2), .in6(_0_2), .in7(Bout_1),
    .out(Y_2), .sel(A_B_C));  // open: en

  // Notes on the sheet:
  //   DIFFERENCE
  //   BORROW
endmodule
